# Fritzing sketch ex13_serial_receiver_lcd (saved by Fritzing 1.0.4)
breadboards: 1

parts:
  LCD1 = LCD screen
  R1 = Resistor [tolerance=±5% resistance=220 package="0805 [SMD]"]
  Part1 = Arduino Uno (Rev3) - ICSP
  R2 = Resistor [tolerance=±5% resistance=220 package="0805 [SMD]"]
  Part2 = Arduino Uno (Rev3) - ICSP

nets:
  GND: LCD1.VSS, LCD1.R/W, Part1.GND, R2.Pin_1, Part2.GND
  VDD: LCD1.VDD, R1.Pin_1, Part1.5V
  N1: LCD1.V0, R2.Pin_0
  N2: LCD1.RS, Part1.D12/MISO
  N3: LCD1.E, Part1.D13/SCK
  N4: LCD1.DB4, Part1.D5_PWM
  N5: LCD1.DB5, Part1.D4
  N6: LCD1.DB6, Part1.D3_PWM
  N7: LCD1.DB7, Part1.D2
  N8: LCD1.LED+, R1.Pin_0
  N9: Part1.ICSP_MOSI, Part1.D11_PWM/MOSI, Part2.D10_PWM/SS
  N10: Part1.D10_PWM/SS, Part2.D11_PWM/MOSI
